// Logisim project cpu.circ as structural Verilog: 5 circuits, main circuit main
module main (
  input  [31:0] INSTRUCTION,
  input  CLOCK,
  output [31:0] FETCH_ADDRESS,
  output [31:0] s0_Value,
  output [31:0] s1_Value,
  output [31:0] t0_Value,
  output [31:0] t1_Value,
  output [31:0] a0_Value,
  output [31:0] ra_Value,
  output [31:0] sp_Value,
  output [31:0] out_11,
  output [31:0] out_12,
  output [31:0] out_13,
  output [31:0] out_14,
  output [31:0] out_15
);

  wire ASel, BrEq, BrLT, BrUn, BSel, FastPCSel, MemRW, PCSel, RegWEn;
  wire [1:0] WBSel;
  wire [2:0] ImmSel;
  wire [3:0] ALUSel;
  wire [6:0] func7;
  wire [11:0] ByteOffset;
  wire [31:0] adder_2_out, ALU, Full_Word, jump, MemWrite, multiplexer_1_out, multiplexer_2_out,
       multiplexer_3_out, NewPC, PC, R1, R2, R_immediate, WriteBack, X, Y;

  Comparator #(.width(7), .mode("unsigned")) comparator_1 (.a(func7), .b(7'b1100110), .gt(FastPCSel));  // open: eq, lt
  Adder #(.width(32)) adder_1 (.a(32'h4), .b(PC), .out(out_13));  // open: cin, cout
  Adder #(.width(32)) adder_2 (.a(32'h1), .b(FETCH_ADDRESS), .out(adder_2_out));  // open: cin, cout
  Bit_Extender #(.in_width(32), .out_width(7)) bit_extender_1 (.in(INSTRUCTION), .out(func7));
  Multiplexer #(.width(32), .disabled(0), .enable("false")) multiplexer_1 (
    .in0(adder_2_out), .in1(jump), .out(multiplexer_1_out), .sel(PCSel));
  Divider #(.width(32)) divider_1 (.a(ALU), .b(32'h4), .out(jump));  // open: upper, rem
  Multiplexer #(.width(32), .enable("false")) multiplexer_2 (
    .in0(INSTRUCTION), .in1({32{1'b0}}), .out(multiplexer_2_out), .sel(PCSel));
  Multiplexer #(.width(32), .enable("false")) multiplexer_3 (
    .in0(out_13), .in1(ALU), .out(multiplexer_3_out), .sel(PCSel));
  Register #(.width(32)) register_1 (.D(multiplexer_3_out), .Q(PC), .clk(CLOCK));  // open: en, clr
  Register #(.width(32)) register_2 (.D(multiplexer_1_out), .Q(FETCH_ADDRESS), .clk(CLOCK));  // open: en, clr
  Multiplexer #(.width(32), .enable("false")) multiplexer_4 (.in0(PC), .in1(out_13), .out(NewPC), .sel(FastPCSel));
  Register #(.width(32)) register_3 (.D(multiplexer_2_out), .Q(out_15), .clk(CLOCK));  // open: en, clr
  Register #(.width(32)) register_4 (.D(PC), .Q(out_12), .clk(CLOCK));  // open: en, clr
  regfile_main main_1 (
    .Read_Register_1__rs1(out_15[19:15]), .Read_Register_2__rs2(out_15[24:20]),
    .Write_Register__rd(out_15[11:7]), .Write_Data(WriteBack), .Write_Enable(RegWEn), .Clock(CLOCK),
    .Read_Data_1(R1), .Read_Data_2(R2), .s1_Value(s1_Value), .t0_Value(t0_Value), .t1_Value(t1_Value),
    .a0_Value(a0_Value), .s0_Value(s0_Value), .ra_Value(ra_Value), .sp_Value(sp_Value));
  Immediate_Generator immediate_generator_1 (
    .INSTRUCTION(out_15), .ImmSel(ImmSel), .R_immediate(R_immediate), .ByteOffset(ByteOffset));
  Branch_Comparator branch_comparator_1 (.r1(R1), .r2(R2), .BrUn(BrUn), .BrEq(BrEq), .BrLT(BrLT));
  Control_Logic control_logic_1 (
    .PCSel(PCSel), .Instruction(out_15), .ImmSel(ImmSel), .RegWEn(RegWEn), .BrUn(BrUn), .BrEq(BrEq),
    .BrLT(BrLT), .BSel(BSel), .ASel(ASel), .ALUSel(ALUSel), .MemRW(MemRW), .WBSel(WBSel));
  Multiplexer #(.width(32), .enable("false")) multiplexer_5 (.in0(R1), .in1(out_12), .out(X), .sel(ASel));
  Multiplexer #(.width(32), .enable("false")) multiplexer_6 (.in0(R2), .in1(R_immediate), .out(Y), .sel(BSel));
  alu_main main_2 (.Switch(ALUSel), .X(X), .Result(ALU), .Y(Y));  // open: Equal
  Load_Generator load_generator_1 (
    .Word_Value(Full_Word), .Byte_Offset(ByteOffset), .INSTRUCTION2(out_15), .MemWrite(MemWrite));
  mem_main MEM (.Address(ALU), .Write_Data(R2), .Write_En(MemRW), .Clock(CLOCK), .Read_Data(Full_Word));
  Multiplexer #(.select(2), .width(32), .enable("false")) multiplexer_7 (
    .in0(MemWrite), .in1(ALU), .in2(NewPC), .in3(R_immediate), .out(WriteBack), .sel(WBSel));

  assign out_11 = FETCH_ADDRESS;
  assign out_14 = INSTRUCTION;

  // Other names for the same wires on the sheet: a0[31:0] = a0_Value; clk = CLOCK; FastPC[31:0] = out_13;
  //   fetch_addr[31:0] = FETCH_ADDRESS; INSTRUCTION2[31:0] = out_15; rd[4:0] = out_15[11:7]; rs1[4:0] = out_15[19:15];
  //   rs2[4:0] = out_15[24:20]; PC___4[31:0] = out_12; ra[31:0] = ra_Value; s0[31:0] = s0_Value; s1[31:0] = s1_Value;
  //   sp[31:0] = sp_Value; t0[31:0] = t0_Value; t1[31:0] = t1_Value

  // Notes on the sheet:
  //   Pipelining
  //   Instruction Fetch
  //   Output
  //   These are outputs/inputs from run.circ
  //   Inputs
  //   Control Logic
  //   Peeker
  //   Instruction Decode
  //   Immediate Generator
  //   These are DEBUG/TEST outputs from your circuit.
  //   Branch Comparator
  //   Execute
  //   Read/Write
  //   Write Back
  //   Load Generator
endmodule

module Control_Logic (
  input  BrEq,
  input  BrLT,
  input  [31:0] Instruction,
  output PCSel,
  output [2:0] ImmSel,
  output RegWEn,
  output BrUn,
  output BSel,
  output ASel,
  output [3:0] ALUSel,
  output MemRW,
  output [1:0] WBSel
);

  wire SBSel_PC, SBSel_Un;
  wire [1:0] bit_extender_1_out;
  wire [2:0] func3;
  wire [3:0] itype, rtype, rtype_func7_0, rtype_func7_1, rtype_func7_4, rtype_func7_6;
  wire [4:0] opcode;
  wire [11:0] bit_extender_2_out;

  Multiplexer #(.select(2), .width(4), .enable("false")) multiplexer_1 (
    .in0(4'b0010), .in1(4'b0111), .in2(4'b1011), .out(rtype_func7_0), .sel({Instruction[31], Instruction[25]}));  // open: in3
  Multiplexer #(.select(2), .width(4), .enable("false")) multiplexer_2 (
    .in0(4'b0000), .in1(4'b1000), .out(rtype_func7_1), .sel({Instruction[31], Instruction[25]}));  // open: in2, in3
  Multiplexer #(.select(2), .width(4), .enable("false")) multiplexer_3 (
    .in0(4'b0101), .in1(4'b1001), .out(rtype_func7_4), .sel({Instruction[31], Instruction[25]}));  // open: in2, in3
  Multiplexer #(.select(2), .width(4), .enable("false")) multiplexer_4 (
    .in0(4'b0100), .in1(4'b1010), .out(rtype_func7_6), .sel({Instruction[31], Instruction[25]}));  // open: in2, in3
  Bit_Extender #(.in_width(32), .out_width(7)) bit_extender_1 (.in(Instruction), .out({opcode, bit_extender_1_out}));
  Bit_Extender #(.in_width(32), .out_width(15)) bit_extender_2 (.in(Instruction), .out({func3, bit_extender_2_out}));
  Multiplexer #(.select(5), .enable("false")) multiplexer_5 (
    .in0(1'b0), .in4(1'b0), .in8(1'b0), .in12(1'b0), .in13(1'b0), .in24(SBSel_PC), .in25(1'b1), .in27(1'b1),
    .out(PCSel), .sel(opcode));  // open: in1, in2, in3, in5, in6, in7, in9, in10, in11, in14, in15, in16, in17, in18, in19, in20, in21, in22, in23, in26, in28, in29, in30, in31
  Multiplexer #(.select(5), .width(3), .enable("false")) multiplexer_6 (
    .in0(3'b101), .in4(3'b000), .in8(3'b001), .in12(3'b011), .in13(3'b011), .in24(3'b010), .in25(3'b000),
    .in27(3'b100), .out(ImmSel), .sel(opcode));  // open: in1, in2, in3, in5, in6, in7, in9, in10, in11, in14, in15, in16, in17, in18, in19, in20, in21, in22, in23, in26, in28, in29, in30, in31
  Multiplexer #(.select(3), .width(4), .enable("false")) multiplexer_7 (
    .in0(rtype_func7_0), .in1(rtype_func7_1), .in2(4'b0110), .in4(rtype_func7_4), .in5(4'b0001),
    .in6(rtype_func7_6), .in7(4'b0011), .out(rtype), .sel(func3));  // open: in3
  Multiplexer #(.select(3), .width(4), .enable("false")) multiplexer_8 (
    .in0(4'b0010), .in1(4'b0000), .in2(4'b0110), .in4(4'b0101), .in5(4'b0001), .in6(4'b0101), .in7(4'b0011),
    .out(itype), .sel(func3));  // open: in3
  Multiplexer #(.select(5), .enable("false")) multiplexer_9 (
    .in0(1'b1), .in4(1'b1), .in8(1'b0), .in12(1'b1), .in13(1'b1), .in24(1'b0), .in25(1'b1), .in27(1'b1),
    .out(RegWEn), .sel(opcode));  // open: in1, in2, in3, in5, in6, in7, in9, in10, in11, in14, in15, in16, in17, in18, in19, in20, in21, in22, in23, in26, in28, in29, in30, in31
  Multiplexer #(.select(5), .width(4), .enable("false")) multiplexer_10 (
    .in0(4'b0010), .in4(itype), .in8(4'b0010), .in12(rtype), .in13(4'b0010), .in24(4'b0010), .in25(4'b0010),
    .in27(4'b0010), .out(ALUSel), .sel(opcode));  // open: in1, in2, in3, in5, in6, in7, in9, in10, in11, in14, in15, in16, in17, in18, in19, in20, in21, in22, in23, in26, in28, in29, in30, in31
  Multiplexer #(.select(5), .disabled(0), .enable("false")) multiplexer_11 (
    .in0(1'b0), .in4(1'b0), .in8(1'b0), .in12(1'b0), .in13(1'b0), .in24(SBSel_Un), .in25(1'b0), .in27(1'b0),
    .out(BrUn), .sel(opcode));  // open: in1, in2, in3, in5, in6, in7, in9, in10, in11, in14, in15, in16, in17, in18, in19, in20, in21, in22, in23, in26, in28, in29, in30, in31
  Multiplexer #(.select(3), .enable("false")) multiplexer_12 (
    .in0(1'b0), .in1(1'b0), .in2(1'b0), .in3(1'b0), .in4(1'b0), .in5(1'b0), .in6(1'b1), .in7(1'b0),
    .out(SBSel_Un), .sel(func3));
  Multiplexer #(.select(5), .disabled(0), .enable("false")) multiplexer_13 (
    .in0(1'b1), .in4(1'b1), .in8(1'b1), .in12(1'b0), .in13(1'b1), .in24(1'b1), .in25(1'b1), .in27(1'b1),
    .out(BSel), .sel(opcode));  // open: in1, in2, in3, in5, in6, in7, in9, in10, in11, in14, in15, in16, in17, in18, in19, in20, in21, in22, in23, in26, in28, in29, in30, in31
  Multiplexer #(.select(5), .disabled(0), .enable("false")) multiplexer_14 (
    .in0(1'b0), .in4(1'b0), .in8(1'b0), .in12(1'b0), .in13(1'b0), .in24(1'b1), .in25(1'b0), .in27(1'b1),
    .out(ASel), .sel(opcode));  // open: in1, in2, in3, in5, in6, in7, in9, in10, in11, in14, in15, in16, in17, in18, in19, in20, in21, in22, in23, in26, in28, in29, in30, in31
  Multiplexer #(.select(5), .disabled(0), .enable("false")) multiplexer_15 (
    .in0(1'b0), .in4(1'b0), .in8(1'b1), .in12(1'b0), .in13(1'b0), .in24(1'b0), .in25(1'b0), .in27(1'b0),
    .out(MemRW), .sel(opcode));  // open: in1, in2, in3, in5, in6, in7, in9, in10, in11, in14, in15, in16, in17, in18, in19, in20, in21, in22, in23, in26, in28, in29, in30, in31
  Multiplexer #(.select(3), .enable("false")) multiplexer_16 (
    .in0(BrEq), .in1(1'b0), .in2(1'b0), .in3(1'b0), .in4(BrLT), .in5(1'b0), .in6(BrLT), .in7(1'b0),
    .out(SBSel_PC), .sel(func3));
  Multiplexer #(.select(5), .width(2), .disabled(0), .enable("false")) multiplexer_17 (
    .in0(2'b00), .in4(2'b01), .in8(2'b00), .in12(2'b01), .in13(2'b11), .in24(2'b00), .in25(2'b10),
    .in27(2'b10), .out(WBSel), .sel(opcode));  // open: in1, in2, in3, in5, in6, in7, in9, in10, in11, in14, in15, in16, in17, in18, in19, in20, in21, in22, in23, in26, in28, in29, in30, in31

  // Other names for the same wires on the sheet: func7[1:0] = {Instruction[31], Instruction[25]}

  // Notes on the sheet:
  //   CONTROL LOGIC
  //   Decode
  //   func7 = 1:6
  //   Selectors
  //   ALUSel
  //   Opcode
  //   r type 12 (0011 0011)
  //   load 0 (0000 0011)
  //   i type 4 (0001 0011)
  //   s type 8 (0010 0011)
  //   sb type 24 (0110 0011)
  //   u type 13 (0011 0111)
  //   uj type 27 (0110 1111)
  //   jalr 25 (0110 0111)
  //   ImmSel
  //   i type = 0
  //   s type = 1
  //   sb type = 2
  //   u type = 3
  //   uj type = 4
  //   l type = 5
  //   BrUn
  //   ALU Sel
  //   sll = 0
  //   srl = 1
  //   add = 2
  //   and = 3
  //   or = 4
  //   xor = 5
  //   slt = 6
  //   mult = 7
  //   mulh = 8
  //   div = 9
  //   rem = a
  //   sub = b
  //   PCSel
endmodule

module Immediate_Generator (
  input  [2:0] ImmSel,
  input  [31:0] INSTRUCTION,
  output [31:0] R_immediate,
  output [11:0] ByteOffset
);

  wire [11:0] divider_1_out;
  wire [31:0] bit_extender_4_out, bit_extender_5_out, itype, jtype, ltype, sbtype, stype;

  assign itype = {{20{INSTRUCTION[31]}}, INSTRUCTION[31:20]};  // Bit_Extender bit_extender_1
  Divider #(.width(12)) divider_1 (
    .a(INSTRUCTION[31:20]), .b(12'h4), .out(divider_1_out), .rem(ByteOffset));  // open: upper
  assign stype = {{20{INSTRUCTION[31]}}, {INSTRUCTION[31:25], INSTRUCTION[11:7]}};  // Bit_Extender bit_extender_2
  assign ltype = {{20{divider_1_out[11]}}, divider_1_out};  // Bit_Extender bit_extender_3
  assign bit_extender_4_out = {{20{INSTRUCTION[31]}}, {INSTRUCTION[31], INSTRUCTION[7], INSTRUCTION[30:25], INSTRUCTION[11:8]}};  // Bit_Extender bit_extender_4
  Shifter #(.width(32)) shifter_1 (.in(bit_extender_4_out), .\dist (5'b00001), .out(sbtype));
  assign bit_extender_5_out = {{12{INSTRUCTION[31]}}, {INSTRUCTION[31], INSTRUCTION[19:12], INSTRUCTION[20], INSTRUCTION[30:21]}};  // Bit_Extender bit_extender_5
  Multiplexer #(.select(3), .width(32), .enable("false")) multiplexer_1 (
    .in0(itype), .in1(stype), .in2(sbtype), .in3({INSTRUCTION[31:12], {12{1'b0}}}), .in4(jtype), .in5(ltype),
    .out(R_immediate), .sel(ImmSel));  // open: in6, in7
  Shifter #(.width(32)) shifter_2 (.in(bit_extender_5_out), .\dist (5'b00001), .out(jtype));

  // Other names for the same wires on the sheet: bit11 = INSTRUCTION[7]; bit1_10[9:0] = INSTRUCTION[30:21];
  //   utype[31:12] = INSTRUCTION[31:12]; bit12_19[7:0] = INSTRUCTION[19:12]; bit12 = INSTRUCTION[31];
  //   out[31:0] = R_immediate

  // Notes on the sheet:
  //   Input
  //   Reconstructed Immediate
  //   Output
  //   ImmSel
  //   i type = 0
  //   s type = 1
  //   sb type = 2
  //   u type = 3
  //   j type = 4
  //   l type = 5
endmodule

module Branch_Comparator (
  input  BrUn,
  input  [31:0] r1,
  input  [31:0] r2,
  output BrEq,
  output BrLT
);

  wire SiLT, UnLT;

  Comparator #(.width(32), .mode("unsigned")) comparator_1 (.a(r1), .b(r2), .eq(BrEq), .lt(UnLT));  // open: gt
  Comparator #(.width(32)) comparator_2 (.a(r1), .b(r2), .lt(SiLT));  // open: gt, eq
  Multiplexer #(.enable("false")) multiplexer_1 (.in0(SiLT), .in1(UnLT), .out(BrLT), .sel(BrUn));

  // Other names for the same wires on the sheet: rs1[31:0] = r1; rs2[31:0] = r2

  // Notes on the sheet:
  //   Input
  //   Branch Comparator
  //   Output
endmodule

module Load_Generator (
  input  [11:0] Byte_Offset,
  input  [31:0] Word_Value,
  output [31:0] INSTRUCTION2,
  output [31:0] MemWrite
);

  wire [1:0] Byte_Offset_t, func3;
  wire [7:0] multiplexer_2_out;
  wire [14:0] bit_extender_2_out;
  wire [15:0] multiplexer_1_out;
  wire [31:0] Byte_Value, Half_Value, Word_4;

  Bit_Extender #(.in_width(12), .out_width(2)) bit_extender_1 (.in(Byte_Offset), .out(Byte_Offset_t));
  Bit_Extender #(.in_width(32), .out_width(15)) bit_extender_2 (
    .in(INSTRUCTION2), .out({bit_extender_2_out[14], func3, bit_extender_2_out[11:0]}));
  Multiplexer #(.select(2), .width(16), .enable("false")) multiplexer_1 (
    .in0(Word_Value[15:0]), .in2(Word_Value[31:16]), .out(multiplexer_1_out), .sel(Byte_Offset_t));  // open: in1, in3
  Multiplexer #(.select(2), .width(8), .enable("false")) multiplexer_2 (
    .in0(Word_Value[7:0]), .in1(Word_Value[15:8]), .in2(Word_Value[23:16]), .in3(Word_Value[31:24]),
    .out(multiplexer_2_out), .sel(Byte_Offset_t));
  assign Half_Value = {{16{multiplexer_1_out[15]}}, multiplexer_1_out};  // Bit_Extender bit_extender_3
  assign Byte_Value = {{24{multiplexer_2_out[7]}}, multiplexer_2_out};  // Bit_Extender bit_extender_4
  Multiplexer #(.select(2), .width(32), .enable("false")) multiplexer_3 (
    .in0(Byte_Value), .in1(Half_Value), .in2(Word_4), .in3({32{1'b0}}), .out(MemWrite), .sel(func3));

  // Other names for the same wires on the sheet: Byte_0[7:0] = Word_Value[7:0]; Half_0[15:0] = Word_Value[15:0];
  //   Byte_1[7:0] = Word_Value[15:8]; Byte_2[7:0] = Word_Value[23:16]; Half_2[15:0] = Word_Value[31:16];
  //   Byte_3[7:0] = Word_Value[31:24]; INSTRUCTION[31:0] = INSTRUCTION2

  // Notes on the sheet:
  //   Input
  //   Word Decode 
  //   func3
  //   lb = 0
  //   lh = 1
  //   Value Select 
  //   lw = 2
  //   Output
endmodule
